// Logisim project alu.circ as structural Verilog: 1 circuit, main circuit ALU
module ALU (
  input  [31:0] A,
  input  [31:0] B,
  input  [3:0] ALU_Op,
  input  [3:0] in_4,
  output [31:0] Out
);

  wire [31:0] adder_1_out, and_1_out, divider_1_out, divider_1_rem, multiplier_1_out, or_1_out,
       shifter_1_out, shifter_2_out, subtractor_1_out, xor_1_out;

  Adder #(.width(32)) adder_1 (.a(A), .b(B), .out(adder_1_out), .cin(1'b0));  // open: cout
  Subtractor #(.width(32)) subtractor_1 (.a(A), .b(B), .out(subtractor_1_out), .bin(1'b0));  // open: bout
  assign and_1_out = A & B;  // AND_Gate and_1, 32 bits wide
  Shifter #(.width(32)) shifter_1 (.in(A), .\dist (B[4:0]), .out(shifter_1_out));
  Shifter #(.width(32), .shift("lr")) shifter_2 (.in(A), .\dist (B[4:0]), .out(shifter_2_out));
  Multiplier #(.width(32)) multiplier_1 (.a(A), .b(B), .out(multiplier_1_out), .cin({32{1'b0}}));  // open: cout
  assign xor_1_out = A ^ B;  // XOR_Gate xor_1, 32 bits wide
  Divider #(.width(32)) divider_1 (.a(A), .b(B), .out(divider_1_out), .upper({32{1'b0}}), .rem(divider_1_rem));
  assign or_1_out = A | B;  // OR_Gate or_1, 32 bits wide
  Multiplexer #(.select(4), .width(32)) multiplexer_1 (
    .in6(adder_1_out), .in7(subtractor_1_out), .in8(and_1_out), .in9(shifter_1_out), .in10(shifter_2_out),
    .in11(multiplier_1_out), .in12(xor_1_out), .in13(divider_1_out), .in14(divider_1_rem), .in15(or_1_out),
    .out(Out), .sel(in_4), .en(1'b0));  // open: in0, in1, in2, in3, in4, in5

  // Other names for the same wires on the sheet: Op[3:0] = ALU_Op

  // Notes on the sheet:
  //   Inputs
  //   NOTE
  //   Please do not modify/replace/move/change/delete/etc input and output pins
  //   Outputs
endmodule
