// Logisim project cpu.circ as structural Verilog: 2 circuits, main circuit CPU
module CPU (
  input  [31:0] Instruction,
  input  CLK,
  output [31:0] s0,
  output [31:0] s1,
  output [31:0] t0,
  output [31:0] t1,
  output [31:0] a0,
  output [31:0] ra,
  output [31:0] sp,
  output [31:0] PC
);

  wire main_1_p1;
  wire [4:0] pc_1_p4, pc_1_p5;
  wire [31:0] alu_1_out, incrementer_1_p1, incrementer_1_p2, multiplexer_1_out, multiplexer_2_out,
       regfile_1_r1, regfile_1_r2, regfile_1_t1;

  // Incrementer incrementer_1: pin names not known; wires that end beside it: incrementer_1_p1, incrementer_1_p2
  Multiplexer #(.width(32)) multiplexer_1 (
    .in0(incrementer_1_p2), .in1(alu_1_out), .out(multiplexer_1_out));  // open: sel, en
  // PC pc_1: pin names not known; wires that end beside it: multiplexer_1_out, CLK, incrementer_1_p1, pc_1_p4, pc_1_p5
  Multiplexer #(.width(32)) multiplexer_2 (
    .in0(incrementer_1_p1), .in1(regfile_1_r1), .out(multiplexer_2_out));  // open: sel, en
  RegFile regfile_1 (
    .Clk(CLK), .R1(regfile_1_r1), .R2(regfile_1_r2), .W(incrementer_1_p1), .RS1(pc_1_p4), .RS2(pc_1_p5),
    .t1(regfile_1_t1));  // open: WE, RD, s0, s1, t0, a0, ra, sp
  ALU alu_1 (.A(multiplexer_2_out), .B(regfile_1_r2), .Out(alu_1_out));  // open: ALU_Op, in_4
  // memory_main main_1: pin names not known; wires that end beside it: main_1_p1, main_1_p1, alu_1_out
  Multiplexer #(.select(2), .width(32)) multiplexer_3 (
    .in0(incrementer_1_p1), .in1(alu_1_out), .in2(alu_1_out), .out(regfile_1_t1));  // open: in3, sel, en

  // Other names for the same wires on the sheet: fetch_addr[31:0] = PC; INST[31:0] = Instruction

  // Notes on the sheet:
  //   NOTE
  //   Please do not modify/replace/move/change/delete/etc input and output pins
  //   These are debug/test outputs from your circuit
endmodule

module Branch (
);

  wire comparator_1_lt, comparator_2_lt, comparator_3_eq, multiplexer_1_out, multiplexer_2_out,
       multiplexer_3_out, negator_1_out;
  wire [31:0] undriven, undriven_2, undriven_3;

  Comparator #(.width(32)) comparator_1 (.a(undriven), .b(undriven_3), .lt(comparator_1_lt));  // open: gt, eq
  Comparator #(.width(32), .mode("unsigned")) comparator_2 (
    .a(undriven), .b(undriven_3), .lt(comparator_2_lt));  // open: gt, eq
  Comparator #(.width(32)) comparator_3 (.a(undriven), .b(undriven_2), .eq(comparator_3_eq));  // open: gt, lt
  Multiplexer multiplexer_1 (.in0(comparator_1_lt), .in1(comparator_2_lt), .out(multiplexer_1_out));  // open: sel, en
  Multiplexer multiplexer_2 (.in0(multiplexer_1_out), .in1(comparator_3_eq), .out(multiplexer_2_out));  // open: sel, en
  Negator #(.width(1)) negator_1 (.in(multiplexer_2_out), .out(negator_1_out));
  Multiplexer multiplexer_3 (.in0(multiplexer_2_out), .in1(negator_1_out), .out(multiplexer_3_out));  // open: sel, en
endmodule
